// Logisim project computer.circ as structural Verilog: 11 circuits, main circuit Central processing unit
module Computer (
);

  wire central_processing_unit_1__16_bit, central_processing_unit_1_get_ram,
       central_processing_unit_1_set_ram;
  wire [15:0] central_processing_unit_1_ram_addres, central_processing_unit_1_ram_output, ram_1_ram_output;

  Central_processing_unit central_processing_unit_1 (
    ._16_bit(central_processing_unit_1__16_bit), .Set_Ram(central_processing_unit_1_set_ram),
    .Get_Ram(central_processing_unit_1_get_ram), .RAM_input(ram_1_ram_output),
    .RAM_Addres(central_processing_unit_1_ram_addres), .RAM_output(central_processing_unit_1_ram_output));
  RAM ram_1 (
    ._16_bit(central_processing_unit_1__16_bit), .Set_Ram(central_processing_unit_1_set_ram),
    .Get_Ram(central_processing_unit_1_get_ram), .RAM_output(ram_1_ram_output),
    .RAM_Addres(central_processing_unit_1_ram_addres), .RAM_input(central_processing_unit_1_ram_output));
endmodule

module RAM (
  input  _16_bit,
  input  Set_Ram,
  input  Get_Ram,
  input  [15:0] RAM_Addres,
  input  [15:0] RAM_input,
  output [15:0] RAM_output
);

  wire button_1_out, button_2_out, nor_1_out, nor_2_out, nor_3_out, nor_4_out, not_1_out, not_2_out;
  wire [7:0] multiplexer_3_out, multiplexer_4_out, ram_1_data, ram_2_data;
  wire [14:0] adder_1_out;

  not not_1 (not_1_out, Set_Ram);
  nor nor_1 (nor_1_out, RAM_Addres[0], _16_bit);
  not not_2 (not_2_out, RAM_Addres[0]);
  nor nor_2 (nor_2_out, not_2_out, _16_bit);
  nor nor_3 (nor_3_out, not_1_out, nor_1_out);
  nor nor_4 (nor_4_out, not_1_out, nor_2_out);
  Adder #(.width(15)) adder_1 (
    .a(RAM_Addres[15:1]), .b({15{1'b0}}), .out(adder_1_out), .cin(RAM_Addres[0]));  // open: cout
  Button button_1 (.out(button_1_out));
  Button button_2 (.out(button_2_out));
  Multiplexer #(.width(8), .enable("false")) multiplexer_1 (
    .in0(ram_2_data), .in1(ram_1_data), .out(RAM_output[7:0]), .sel(RAM_Addres[0]));
  RAM_part #(.addrWidth(15)) ram_1 (
    .addr(RAM_Addres[15:1]), .data(ram_1_data), .clk(nor_3_out), .ld(Get_Ram), .clr(button_1_out));  // open: sel
  RAM_part #(.addrWidth(15)) ram_2 (
    .addr(adder_1_out), .data(ram_2_data), .clk(nor_4_out), .ld(Get_Ram), .clr(button_2_out));  // open: sel
  Multiplexer #(.width(8), .enable("false")) multiplexer_2 (
    .in0(ram_1_data), .in1(ram_2_data), .out(RAM_output[15:8]), .sel(RAM_Addres[0]));
  Multiplexer #(.width(8), .enable("false")) multiplexer_3 (
    .in0(RAM_input[7:0]), .in1(RAM_input[15:8]), .out(multiplexer_3_out), .sel(RAM_Addres[0]));
  assign ram_2_data = Set_Ram ? multiplexer_3_out : 8'bz;  // Controlled_Buffer controlled_buffer_1
  assign ram_1_data = Set_Ram ? multiplexer_4_out : 8'bz;  // Controlled_Buffer controlled_buffer_2
  Multiplexer #(.width(8), .enable("false")) multiplexer_4 (
    .in0(RAM_input[15:8]), .in1(RAM_input[7:0]), .out(multiplexer_4_out), .sel(RAM_Addres[0]));
endmodule

module Central_processing_unit (
  input  [15:0] RAM_input,
  output _16_bit,
  output Set_Ram,
  output Get_Ram,
  output [15:0] RAM_Addres,
  output [15:0] RAM_output
);

  wire arithmetic_logic_unit_1_carry_out, arithmetic_logic_unit_1_overflow, control_unit_1__16_bit,
       control_unit_1__16_bit_2, control_unit_1_carry_in, control_unit_1_get_ram, control_unit_1_set_ram,
       control_unit_1_update_fs;
  wire [2:0] control_unit_1_address_reg_base, control_unit_1_alu_micro_operation;
  wire [3:0] control_unit_1_address_reg_a, control_unit_1_address_reg_b, control_unit_1_reg_address;
  wire [7:0] control_unit_1_output_fs_2, registery_1_fs_out;
  wire [15:0] arithmetic_logic_unit_1_result, control_unit_1_a, control_unit_1_b, control_unit_1_imidiate,
       control_unit_1_input_reg, control_unit_1_ram_output, ram_interface_1_ram_addres_2,
       ram_interface_1_ram_input_2, registery_1_output_a, registery_1_output_b, registery_1_output_base;

  RAM_interface ram_interface_1 (
    .Get_RAM_2(Set_Ram), .Set_RAM_2(Get_Ram), .RAM_input(RAM_input), .RAM_Addres(RAM_output),
    .RAM_output_2(RAM_Addres), ._16_bit(control_unit_1__16_bit_2), .Get_RAM(control_unit_1_get_ram),
    .Set_RAM(control_unit_1_set_ram), .RAM_input_2(ram_interface_1_ram_input_2),
    .Base_address(registery_1_output_base), .RAM_output(control_unit_1_ram_output), ._16_bit_2(_16_bit),
    .Imidiate_address(control_unit_1_imidiate), .RAM_Addres_2(ram_interface_1_ram_addres_2));
  Control_unit control_unit_1 (
    .Carry_In(control_unit_1_carry_in), ._16_bit(control_unit_1__16_bit), .B(control_unit_1_b),
    .A(control_unit_1_a), .ALU_Micro_Operation(control_unit_1_alu_micro_operation),
    .Result(arithmetic_logic_unit_1_result), .Carry_Out(arithmetic_logic_unit_1_carry_out),
    .Overflow_Out(arithmetic_logic_unit_1_overflow), .Output_FS_2(control_unit_1_output_fs_2),
    .Update_FS(control_unit_1_update_fs), .Input_Reg(control_unit_1_input_reg),
    .Reg_Address(control_unit_1_reg_address), .Output_FS(registery_1_fs_out),
    .Output_Reg_A(registery_1_output_a), .Address_Reg_A(control_unit_1_address_reg_a),
    .RAM_output(control_unit_1_ram_output), .RAM_input(ram_interface_1_ram_input_2),
    ._16_bit_2(control_unit_1__16_bit_2), .Get_RAM(control_unit_1_get_ram), .Set_RAM(control_unit_1_set_ram),
    .Output_Reg_B(registery_1_output_b), .Address_Reg_B(control_unit_1_address_reg_b),
    .Address_Reg_Base(control_unit_1_address_reg_base), .Address(ram_interface_1_ram_addres_2),
    .Imidiate(control_unit_1_imidiate));  // open: Clock
  Arithmetic_logic_unit arithmetic_logic_unit_1 (
    .Carry_In(control_unit_1_carry_in), ._16_bit(control_unit_1__16_bit), .A(control_unit_1_a),
    .B(control_unit_1_b), .Micro_Operation(control_unit_1_alu_micro_operation),
    .Result(arithmetic_logic_unit_1_result), .Carry_Out(arithmetic_logic_unit_1_carry_out),
    .Overflow(arithmetic_logic_unit_1_overflow));
  Registery registery_1 (
    .Data_in(control_unit_1_input_reg), .Input_Register(control_unit_1_reg_address),
    .FS_out(registery_1_fs_out), .FS_In(control_unit_1_output_fs_2), .Update_FS(control_unit_1_update_fs),
    .Base_Register(control_unit_1_address_reg_base), .Output_Base(registery_1_output_base),
    .B_Register(control_unit_1_address_reg_b), .Output_B(registery_1_output_b),
    .A_Register(control_unit_1_address_reg_a), .Output_A(registery_1_output_a));
endmodule

module Control_unit (
  input  Clock,
  input  [15:0] RAM_input,
  input  [15:0] Address,
  input  [15:0] Result,
  input  Carry_Out,
  input  Overflow_Out,
  input  [15:0] Output_Reg_A,
  input  [15:0] Output_Reg_B,
  input  [7:0] Output_FS,
  output Carry_In,
  output _16_bit,
  output [15:0] A,
  output _16_bit_2,
  output [15:0] B,
  output Get_RAM,
  output Set_RAM,
  output [15:0] RAM_output,
  output [2:0] ALU_Micro_Operation,
  output [15:0] Imidiate,
  output [15:0] Input_Reg,
  output [2:0] Address_Reg_Base,
  output [3:0] Address_Reg_A,
  output [3:0] Address_Reg_B,
  output [3:0] Reg_Address,
  output Update_FS,
  output [7:0] Output_FS_2
);

  wire control_stage_counter_1_excecute_op, control_stage_counter_1_save_a, Load_A, Load_B, Load_Imidiate,
       Load_Instruction, Next, not_1_out;
  wire [2:0] multiplexer_2_out;
  wire [15:0] Imidiate_q, Instruction_q, Y_in;

  Register #(.width(16), .trigger("high")) Instruction (
    .D(RAM_input), .Q({Instruction_q[15:11], _16_bit, Instruction_q[9:0]}), .clk(Load_Instruction));  // open: en, clr
  Register #(.width(16), .trigger("high")) u_Imidiate (
    .D(RAM_input), .Q(Imidiate_q), .clk(Load_Imidiate));  // open: en, clr
  Multiplexer #(.width(16), .enable("false")) multiplexer_1 (.in0(Imidiate_q), .in1(16'h2), .out(Imidiate), .sel(Next));
  Control_Stage_Counter control_stage_counter_1 (
    .Clock(Clock), .B_mode(Instruction_q[7]), .Load_Instruction(Load_Instruction),
    .Load_Imidiate(Load_Imidiate), .Load_B(Load_B), .Load_A(Load_A),
    .Excecute_OP(control_stage_counter_1_excecute_op), .Save_A(control_stage_counter_1_save_a),
    .A_mode(Instruction_q[6]));
  not not_1 (not_1_out, Load_B);
  Multiplexer #(.width(3), .enable("false")) multiplexer_2 (
    .in0({Instruction_q[15], Instruction_q[13:12]}), .in1({Instruction_q[11], Instruction_q[9:8]}),
    .out(multiplexer_2_out), .sel(not_1_out));
  Multiplexer #(.width(3), .enable("false")) multiplexer_3 (
    .in0(multiplexer_2_out), .in1(3'b100), .out(Address_Reg_Base), .sel(Next));
  or or_1 (Next, Load_Instruction, Load_Imidiate);
  Multiplexer #(.width(4), .enable("false")) multiplexer_4 (
    .in0({Instruction_q[11], _16_bit, Instruction_q[9:8]}), .in1(4'b1110), .out(Address_Reg_A),
    .sel(Instruction_q[6]));
  Multiplexer #(.width(4), .enable("false")) multiplexer_5 (
    .in0(Instruction_q[15:12]), .in1(4'b1111), .out(Address_Reg_B), .sel(Instruction_q[7]));
  Condition_Check condition_check_1 (.Condition(Instruction_q[3:0]), .Flags(Output_FS));  // open: Truth
  Value_Tester value_tester_1 (
    .Test_Reg(Y_in), ._16_bit(_16_bit), .Overflow(Overflow_Out), .Carry(Carry_Out), .Flags_In(Output_FS),
    .Flags_Out(Output_FS_2));

  assign _16_bit_2 = _16_bit;
  assign A = Output_Reg_A;
  assign B = Output_Reg_B;
  assign RAM_output = Output_Reg_B;

  // Other names for the same wires on the sheet: _16 = _16_bit; Carry = Carry_In; FS[7:0] = Output_FS;
  //   Reg_A[3:0] = Address_Reg_A; Reg_B[3:0] = Address_Reg_B; Test = Update_FS
endmodule

module Registery (
  input  [3:0] B_Register,
  input  [3:0] A_Register,
  input  [2:0] Base_Register,
  input  [15:0] Data_in,
  input  [3:0] Input_Register,
  input  [7:0] FS_In,
  input  Update_FS,
  output [7:0] FS_out,
  output [15:0] Output_B,
  output [15:0] Output_A,
  output [15:0] Output_Base
);

  wire decoder_1_out0, decoder_1_out1, decoder_1_out2, decoder_1_out3, decoder_1_out4, decoder_1_out5,
       decoder_1_out6, decoder_1_out7, decoder_1_out8, decoder_1_out9, decoder_1_out12, decoder_1_out13,
       decoder_1_out14, decoder_1_out15, or_1_out, or_2_out, or_3_out, or_4_out, or_5_out;
  wire [7:0] AH_q, AL_q, BH_q, BL_q, IS_q, multiplexer_4_out, multiplexer_5_out, multiplexer_6_out;
  wire [15:0] AS_q, BS_q, CS_q, CX_q, DX_q, SS_q;

  Multiplexer #(.select(4), .width(16), .enable("false")) multiplexer_1 (
    .in0({{8{1'b0}}, AL_q}), .in1({{8{1'b0}}, AH_q}), .in2({{8{1'b0}}, BL_q}), .in3({{8{1'b0}}, BH_q}),
    .in4({AH_q, AL_q}), .in5({BH_q, BL_q}), .in6(CX_q), .in7(DX_q), .in8({{8{1'b0}}, FS_out}),
    .in9({{8{1'b0}}, IS_q}), .in10({16{1'b0}}), .in11(16'h1), .in12(CS_q), .in13(SS_q), .in14(AS_q),
    .in15(BS_q), .out(Output_B), .sel(B_Register));
  Multiplexer #(.select(4), .width(16), .enable("false")) multiplexer_2 (
    .in0({{8{1'b0}}, AL_q}), .in1({{8{1'b0}}, AH_q}), .in2({{8{1'b0}}, BL_q}), .in3({{8{1'b0}}, BH_q}),
    .in4({AH_q, AL_q}), .in5({BH_q, BL_q}), .in6(CX_q), .in7(DX_q), .in8({{8{1'b0}}, FS_out}),
    .in9({{8{1'b0}}, IS_q}), .in10({16{1'b0}}), .in11(16'h1), .in12(CS_q), .in13(SS_q), .in14(AS_q),
    .in15(BS_q), .out(Output_A), .sel(A_Register));
  Multiplexer #(.select(3), .width(16), .enable("false")) multiplexer_3 (
    .in0({AH_q, AL_q}), .in1({BH_q, BL_q}), .in2(CX_q), .in3(DX_q), .in4(CS_q), .in5(SS_q), .in6({16{1'b0}}),
    .in7(16'h1), .out(Output_Base), .sel(Base_Register));
  Register #(.width(16), .trigger("high")) BS (.D(Data_in), .Q(BS_q), .clk(decoder_1_out15));  // open: en, clr
  Register #(.width(16), .trigger("high")) AS (.D(Data_in), .Q(AS_q), .clk(decoder_1_out14));  // open: en, clr
  Register #(.width(16), .trigger("high")) SS (.D(Data_in), .Q(SS_q), .clk(decoder_1_out13));  // open: en, clr
  Register #(.width(16), .trigger("high")) CS (.D(Data_in), .Q(CS_q), .clk(decoder_1_out12));  // open: en, clr
  Register #(.trigger("high")) IS (.D(Data_in[7:0]), .Q(IS_q), .clk(decoder_1_out9));  // open: en, clr
  Multiplexer #(.width(8), .enable("false")) multiplexer_4 (
    .in0(FS_In), .in1(Data_in[7:0]), .out(multiplexer_4_out), .sel(decoder_1_out8));
  Register #(.trigger("high")) FS (.D(multiplexer_4_out), .Q(FS_out), .clk(or_1_out));  // open: en, clr
  or or_1 (or_1_out, Update_FS, decoder_1_out8);
  Register #(.width(16), .trigger("high")) DX (.D(Data_in), .Q(DX_q), .clk(decoder_1_out7));  // open: en, clr
  Register #(.width(16), .trigger("high")) CX (.D(Data_in), .Q(CX_q), .clk(decoder_1_out6));  // open: en, clr
  Multiplexer #(.width(8), .enable("false")) multiplexer_5 (
    .in0(Data_in[7:0]), .in1(Data_in[15:8]), .out(multiplexer_5_out), .sel(decoder_1_out5));
  Register #(.trigger("high")) BH (.D(multiplexer_5_out), .Q(BH_q), .clk(or_2_out));  // open: en, clr
  or or_2 (or_2_out, decoder_1_out5, decoder_1_out3);
  Register #(.trigger("high")) BL (.D(Data_in[7:0]), .Q(BL_q), .clk(or_3_out));  // open: en, clr
  or or_3 (or_3_out, decoder_1_out5, decoder_1_out2);
  Register #(.trigger("high")) AH (.D(multiplexer_6_out), .Q(AH_q), .clk(or_4_out));  // open: en, clr
  Multiplexer #(.width(8), .enable("false")) multiplexer_6 (
    .in0(Data_in[7:0]), .in1(Data_in[15:8]), .out(multiplexer_6_out), .sel(decoder_1_out4));
  or or_4 (or_4_out, decoder_1_out4, decoder_1_out1);
  Register #(.trigger("high")) AL (.D(Data_in[7:0]), .Q(AL_q), .clk(or_5_out));  // open: en, clr
  or or_5 (or_5_out, decoder_1_out4, decoder_1_out0);
  // Probe on Data_in
  Decoder #(.select(4), .enable("false")) decoder_1 (
    .out0(decoder_1_out0), .out1(decoder_1_out1), .out2(decoder_1_out2), .out3(decoder_1_out3),
    .out4(decoder_1_out4), .out5(decoder_1_out5), .out6(decoder_1_out6), .out7(decoder_1_out7),
    .out8(decoder_1_out8), .out9(decoder_1_out9), .out12(decoder_1_out12), .out13(decoder_1_out13),
    .out14(decoder_1_out14), .out15(decoder_1_out15), .sel(Input_Register));  // open: out10, out11
endmodule

module Arithmetic_logic_unit (
  input  Carry_In,
  input  _16_bit,
  input  [15:0] A,
  input  [15:0] B,
  input  [2:0] Micro_Operation,
  output [15:0] Result,
  output Carry_Out,
  output Overflow
);

  wire adder_1_cout, adder_2_cout, adder_3_cout, adder_4_cout, decoder_1_out0, decoder_1_out1,
       decoder_1_out2, decoder_1_out3, decoder_1_out4, decoder_1_out5, decoder_1_out6, decoder_1_out7,
       multiplexer_1_out, multiplexer_3_out, multiplexer_4_out, multiplexer_5_out, multiplexer_6_out,
       multiplexer_7_out, multiplexer_8_out, multiplexer_9_out, multiplexer_10_out, nor_1_out, nor_2_out,
       subtractor_1_bout, subtractor_2_bout, subtractor_3_bout, subtractor_4_bout, xnor_1_out, xnor_2_out,
       xor_2_out, xor_3_out;
  wire [6:0] adder_1_out, adder_3_out, subtractor_1_out, subtractor_3_out;
  wire [7:7] multiplexer_2_out;
  wire [15:0] and_1_out, not_1_out, or_1_out, xor_1_out;
  wire [15:7] adder_2_out, subtractor_2_out;

  Decoder #(.select(3), .enable("false")) decoder_1 (
    .out0(decoder_1_out0), .out1(decoder_1_out1), .out2(decoder_1_out2), .out3(decoder_1_out3),
    .out4(decoder_1_out4), .out5(decoder_1_out5), .out6(decoder_1_out6), .out7(decoder_1_out7),
    .sel(Micro_Operation));
  Pull_Resistor pull_resistor_1 (.node(Result));
  Pull_Resistor pull_resistor_2 (.node(Carry_Out));
  Pull_Resistor pull_resistor_3 (.node(Overflow));
  assign or_1_out = B | A;  // OR_Gate or_1, 16 bits wide
  assign not_1_out = ~B;  // NOT_Gate not_1, 16 bits wide
  assign Result = decoder_1_out0 ? not_1_out : 16'bz;  // Controlled_Buffer controlled_buffer_1
  assign Result = decoder_1_out1 ? or_1_out : 16'bz;  // Controlled_Buffer controlled_buffer_2
  assign and_1_out = B & A;  // AND_Gate and_1, 16 bits wide
  assign Result = decoder_1_out2 ? and_1_out : 16'bz;  // Controlled_Buffer controlled_buffer_3
  assign xor_1_out = B ^ A;  // XOR_Gate xor_1, 16 bits wide
  assign Result = decoder_1_out3 ? xor_1_out : 16'bz;  // Controlled_Buffer controlled_buffer_4
  Multiplexer #(.enable("false")) multiplexer_1 (.in0(B[7]), .in1(B[15]), .out(multiplexer_1_out), .sel(_16_bit));
  assign Carry_Out = decoder_1_out4 ? multiplexer_1_out : 1'bz;  // Controlled_Buffer controlled_buffer_5
  Multiplexer #(.enable("false")) multiplexer_2 (.in0(Carry_In), .in1(B[8]), .out(multiplexer_2_out[7]), .sel(_16_bit));
  assign Result = decoder_1_out4 ? {B[14:0], Carry_In} : 16'bz;  // Controlled_Buffer controlled_buffer_6
  assign Carry_Out = decoder_1_out5 ? B[0] : 1'bz;  // Controlled_Buffer controlled_buffer_7
  assign Result = decoder_1_out5 ? {Carry_In, B[15:9], multiplexer_2_out[7], B[7:1]} : 16'bz;  // Controlled_Buffer controlled_buffer_8
  Multiplexer #(.enable("false")) multiplexer_3 (.in0(A[7]), .in1(A[15]), .out(multiplexer_3_out), .sel(_16_bit));
  Adder #(.width(7)) adder_1 (.a(B[6:0]), .b(A[6:0]), .out(adder_1_out), .cin(Carry_In), .cout(adder_1_cout));
  Adder #(.width(1)) adder_2 (.a(B[7]), .b(A[7]), .out(adder_2_out[7]), .cin(adder_1_cout), .cout(adder_2_cout));
  Adder #(.width(7)) adder_3 (.a(B[14:8]), .b(A[14:8]), .out(adder_3_out), .cin(adder_2_cout), .cout(adder_3_cout));
  Adder #(.width(1)) adder_4 (.a(B[15]), .b(A[15]), .out(adder_2_out[15]), .cin(adder_3_cout), .cout(adder_4_cout));
  Multiplexer #(.enable("false")) multiplexer_4 (.in0(B[7]), .in1(B[15]), .out(multiplexer_4_out), .sel(_16_bit));
  xor xor_2 (xor_2_out, multiplexer_4_out, multiplexer_3_out);
  Multiplexer #(.enable("false")) multiplexer_5 (
    .in0(adder_2_cout), .in1(adder_4_cout), .out(multiplexer_5_out), .sel(_16_bit));
  assign Carry_Out = decoder_1_out6 ? multiplexer_5_out : 1'bz;  // Controlled_Buffer controlled_buffer_9
  assign Result = decoder_1_out6 ? {adder_2_out[15], adder_3_out, adder_2_out[7], adder_1_out} : 16'bz;  // Controlled_Buffer controlled_buffer_10
  Multiplexer #(.enable("false")) multiplexer_6 (
    .in0(adder_1_cout), .in1(adder_3_cout), .out(multiplexer_6_out), .sel(_16_bit));
  xnor xnor_1 (xnor_1_out, multiplexer_4_out, multiplexer_6_out);
  nor nor_1 (nor_1_out, xor_2_out, xnor_1_out);
  assign Overflow = decoder_1_out6 ? nor_1_out : 1'bz;  // Controlled_Buffer controlled_buffer_11
  Multiplexer #(.enable("false")) multiplexer_7 (.in0(A[7]), .in1(A[15]), .out(multiplexer_7_out), .sel(_16_bit));
  Subtractor #(.width(7)) subtractor_1 (
    .a(B[6:0]), .b(A[6:0]), .out(subtractor_1_out), .bin(Carry_In), .bout(subtractor_1_bout));
  Subtractor #(.width(1)) subtractor_2 (
    .a(B[7]), .b(A[7]), .out(subtractor_2_out[7]), .bin(subtractor_1_bout), .bout(subtractor_2_bout));
  Subtractor #(.width(7)) subtractor_3 (
    .a(B[14:8]), .b(A[14:8]), .out(subtractor_3_out), .bin(subtractor_2_bout), .bout(subtractor_3_bout));
  Subtractor #(.width(1)) subtractor_4 (
    .a(B[15]), .b(A[15]), .out(subtractor_2_out[15]), .bin(subtractor_3_bout), .bout(subtractor_4_bout));
  Multiplexer #(.enable("false")) multiplexer_8 (.in0(B[7]), .in1(B[15]), .out(multiplexer_8_out), .sel(_16_bit));
  Multiplexer #(.enable("false")) multiplexer_9 (
    .in0(subtractor_2_bout), .in1(subtractor_4_bout), .out(multiplexer_9_out), .sel(_16_bit));
  xnor xnor_2 (xnor_2_out, multiplexer_8_out, multiplexer_7_out);
  assign Carry_Out = decoder_1_out7 ? multiplexer_9_out : 1'bz;  // Controlled_Buffer controlled_buffer_12
  assign Result = decoder_1_out7 ? {subtractor_2_out[15], subtractor_3_out, subtractor_2_out[7], subtractor_1_out} : 16'bz;  // Controlled_Buffer controlled_buffer_13
  Multiplexer #(.enable("false")) multiplexer_10 (
    .in0(subtractor_1_bout), .in1(subtractor_3_bout), .out(multiplexer_10_out), .sel(_16_bit));
  xor xor_3 (xor_3_out, multiplexer_8_out, multiplexer_10_out);
  nor nor_2 (nor_2_out, xnor_2_out, xor_3_out);
  assign Overflow = decoder_1_out7 ? nor_2_out : 1'bz;  // Controlled_Buffer controlled_buffer_14

  // Notes on the sheet:
  //   NOT
  //   OR
  //   XOR
  //   AND
  //   LSH
  //   RSH
  //   ADD
  //   SUB
endmodule

module RAM_interface (
  input  _16_bit,
  input  Get_RAM,
  input  Set_RAM,
  input  [15:0] RAM_input,
  input  [15:0] RAM_output,
  input  [15:0] Base_address,
  input  [15:0] Imidiate_address,
  output _16_bit_2,
  output Get_RAM_2,
  output Set_RAM_2,
  output [15:0] RAM_input_2,
  output [15:0] RAM_output_2,
  output [15:0] RAM_Addres,
  output [15:0] RAM_Addres_2
);

  wire not_1_out, not_3_out, not_5_out, not_6_out, not_7_out, not_8_out, not_9_out, not_10_out, not_11_out,
       not_12_out, not_13_out, not_14_out, not_15_out, not_16_out;

  not not_1 (not_1_out, not_5_out);
  not not_2 (Get_RAM_2, not_1_out);
  not not_3 (not_3_out, not_7_out);
  not not_4 (Set_RAM_2, not_3_out);
  not not_5 (not_5_out, not_6_out);
  not not_6 (not_6_out, not_9_out);
  not not_7 (not_7_out, not_8_out);
  not not_8 (not_8_out, not_12_out);
  not not_9 (not_9_out, not_10_out);
  not not_10 (not_10_out, not_13_out);
  not not_11 (not_11_out, not_15_out);
  not not_12 (not_12_out, not_11_out);
  Adder #(.width(16)) adder_1 (.a(Base_address), .b(Imidiate_address), .out(RAM_Addres));  // open: cin, cout
  not not_13 (not_13_out, not_14_out);
  not not_14 (not_14_out, Get_RAM);
  not not_15 (not_15_out, not_16_out);
  not not_16 (not_16_out, Set_RAM);

  assign _16_bit_2 = _16_bit;
  assign RAM_Addres_2 = RAM_Addres;
  assign RAM_input_2 = RAM_input;
  assign RAM_output_2 = RAM_output;
endmodule

module Value_Tester (
  input  Overflow,
  input  Carry,
  input  [7:0] Flags_In,
  input  [15:0] Test_Reg,
  input  _16_bit,
  output [7:0] Flags_Out
);

  nor nor_1 (Flags_Out[0], Test_Reg[0], Test_Reg[1], Test_Reg[2], Test_Reg[3], Test_Reg[4], Test_Reg[5], Test_Reg[6], Test_Reg[7], Test_Reg[8], Test_Reg[9], Test_Reg[10], Test_Reg[11], Test_Reg[12], Test_Reg[13], Test_Reg[14], Test_Reg[15]);
  Multiplexer #(.enable("false")) multiplexer_1 (
    .in0(Test_Reg[7]), .in1(Test_Reg[15]), .out(Flags_Out[1]), .sel(_16_bit));
  not not_1 (Flags_Out[2], Test_Reg[0]);

  assign Flags_Out[7:3] = {Flags_In[7:5], Overflow, Carry};
endmodule

module Condition_Check (
  input  [3:0] Condition,
  input  [7:0] Flags,
  output Truth
);

  wire controlled_buffer_1_out, decoder_1_out0, decoder_1_out1, decoder_1_out2, decoder_1_out3,
       decoder_1_out4, decoder_1_out5, decoder_1_out6, decoder_1_out7, nor_1_out, not_1_out;

  Decoder #(.select(3)) decoder_1 (
    .out0(decoder_1_out0), .out1(decoder_1_out1), .out2(decoder_1_out2), .out3(decoder_1_out3),
    .out4(decoder_1_out4), .out5(decoder_1_out5), .out6(decoder_1_out6), .out7(decoder_1_out7),
    .sel(Condition[3:1]));  // open: en
  not not_1 (not_1_out, Flags[1]);
  nor nor_1 (nor_1_out, not_1_out, Flags[0]);
  assign controlled_buffer_1_out = decoder_1_out0 ? Flags[0] : 1'bz;  // Controlled_Buffer controlled_buffer_1
  assign controlled_buffer_1_out = decoder_1_out1 ? Flags[1] : 1'bz;  // Controlled_Buffer controlled_buffer_2
  assign controlled_buffer_1_out = decoder_1_out2 ? Flags[2] : 1'bz;  // Controlled_Buffer controlled_buffer_3
  assign controlled_buffer_1_out = decoder_1_out3 ? Flags[3] : 1'bz;  // Controlled_Buffer controlled_buffer_4
  assign controlled_buffer_1_out = decoder_1_out4 ? Flags[4] : 1'bz;  // Controlled_Buffer controlled_buffer_5
  assign controlled_buffer_1_out = decoder_1_out5 ? nor_1_out : 1'bz;  // Controlled_Buffer controlled_buffer_6
  assign controlled_buffer_1_out = decoder_1_out6 ? 1'b1 : 1'bz;  // Controlled_Buffer controlled_buffer_7
  assign controlled_buffer_1_out = decoder_1_out7 ? 1'b1 : 1'bz;  // Controlled_Buffer controlled_buffer_8
  xor xor_1 (Truth, Condition[0], controlled_buffer_1_out);
endmodule

module Control_Stage_Counter (
  input  Clock,
  input  B_mode,
  input  A_mode,
  output Load_Instruction,
  output Load_Imidiate,
  output Load_B,
  output Load_A,
  output Excecute_OP,
  output Save_A
);

  wire and_1_out, demultiplexer_1_out0, demultiplexer_1_out1, demultiplexer_2_out0, demultiplexer_2_out1,
       demultiplexer_3_out0, demultiplexer_3_out1, nor_1_out, or_1_out, or_2_out, or_3_out;

  nor nor_1 (nor_1_out, and_1_out, Load_A, Load_B, Load_Imidiate, Load_Instruction);
  D_Flip_Flop d_ff_1 (.clk(Clock), .D(nor_1_out), .Q(Load_Instruction));  // open: Qn, preset, en, reset
  Demultiplexer #(.enable("false")) demultiplexer_1 (
    .out0(demultiplexer_1_out0), .out1(demultiplexer_1_out1), .in(Load_Instruction), .sel(or_1_out));
  or or_1 (or_1_out, A_mode, B_mode);
  D_Flip_Flop d_ff_2 (.clk(Clock), .D(demultiplexer_1_out1), .Q(Load_Imidiate));  // open: Qn, preset, en, reset
  Demultiplexer #(.enable("false")) demultiplexer_2 (
    .out0(demultiplexer_2_out0), .out1(demultiplexer_2_out1), .in(Load_Imidiate), .sel(A_mode));
  D_Flip_Flop d_ff_3 (.clk(Clock), .D(demultiplexer_2_out1), .Q(Load_B));  // open: Qn, preset, en, reset
  Demultiplexer #(.enable("false")) demultiplexer_3 (
    .out0(demultiplexer_3_out0), .out1(demultiplexer_3_out1), .in(Load_B), .sel(B_mode));
  or or_2 (or_2_out, demultiplexer_3_out1, demultiplexer_2_out0);
  D_Flip_Flop d_ff_4 (.clk(Clock), .D(or_2_out), .Q(Load_A));  // open: Qn, preset, en, reset
  D_Flip_Flop d_ff_5 (.clk(Clock), .D(or_3_out), .Q(Excecute_OP));  // open: Qn, preset, en, reset
  or or_3 (or_3_out, demultiplexer_1_out0, demultiplexer_3_out0, Load_A);
  and and_1 (and_1_out, Excecute_OP, A_mode);
  D_Flip_Flop d_ff_6 (.clk(Clock), .D(and_1_out), .Q(Save_A));  // open: Qn, preset, en, reset
endmodule

module Microcode_Logic (
  input  [5:0] OP,
  input  Truth
);

  // Probe on OP
  Multiplexer #(.width(3), .enable("false")) multiplexer_1 (.sel(OP[5]));  // open: in0, in1, out
endmodule
