// Logisim project computer.circ as structural Verilog: 12 circuits, main circuit Central processing unit
module Computer (
  input  Execute,
  input  Reset
);

  wire and_1_out, central_processing_unit_1__16_bit, central_processing_unit_1_get_ram,
       central_processing_unit_1_set_ram, clock_1_out, or_1_out, pre_loader_1_loaded, pre_loader_1_set_ram;
  wire [15:0] central_processing_unit_1_ram_addres, central_processing_unit_1_ram_output, multiplexer_1_out,
       multiplexer_2_out, pre_loader_1_address, pre_loader_1_data, ram_1_ram_output;

  Clock clock_1 (.out(clock_1_out));
  or or_1 (or_1_out, pre_loader_1_set_ram, central_processing_unit_1_set_ram);
  Multiplexer #(.width(16), .enable("false")) multiplexer_1 (
    .in0(pre_loader_1_address), .in1(central_processing_unit_1_ram_addres), .out(multiplexer_1_out),
    .sel(pre_loader_1_loaded));
  Multiplexer #(.width(16), .enable("false")) multiplexer_2 (
    .in0(pre_loader_1_data), .in1(central_processing_unit_1_ram_output), .out(multiplexer_2_out),
    .sel(pre_loader_1_loaded));
  RAM ram_1 (
    ._16_bit(central_processing_unit_1__16_bit), .Set_Ram(or_1_out),
    .Get_Ram(central_processing_unit_1_get_ram), .RAM_output(ram_1_ram_output),
    .RAM_Addres(multiplexer_1_out), .RAM_input(multiplexer_2_out));
  Pre_Loader pre_loader_1 (
    .Clock(clock_1_out), .Reset(Reset), .Loaded(pre_loader_1_loaded), .Set_RAM(pre_loader_1_set_ram),
    .Address(pre_loader_1_address), .Data(pre_loader_1_data));
  and and_1 (and_1_out, pre_loader_1_loaded, clock_1_out, Execute);
  Central_processing_unit central_processing_unit_1 (
    ._16_bit(central_processing_unit_1__16_bit), .RAM_input(ram_1_ram_output),
    .RAM_Addres(central_processing_unit_1_ram_addres), .RAM_output(central_processing_unit_1_ram_output),
    .Get_Ram(central_processing_unit_1_get_ram), .Set_Ram(central_processing_unit_1_set_ram),
    .Clock(and_1_out), .Reset(Reset));
endmodule

module RAM (
  input  _16_bit,
  input  Get_Ram,
  input  Set_Ram,
  input  [15:0] RAM_Addres,
  input  [15:0] RAM_input,
  output [15:0] RAM_output
);

  wire button_1_out, button_2_out, nor_1_out, nor_2_out, nor_3_out, nor_4_out, not_1_out, not_2_out;
  wire [7:0] multiplexer_3_out, multiplexer_4_out, ram_1_data, ram_2_data;
  wire [14:0] adder_1_out;

  not not_1 (not_1_out, Set_Ram);
  nor nor_1 (nor_1_out, RAM_Addres[0], _16_bit);
  not not_2 (not_2_out, RAM_Addres[0]);
  nor nor_2 (nor_2_out, not_2_out, _16_bit);
  nor nor_3 (nor_3_out, not_1_out, nor_1_out);
  nor nor_4 (nor_4_out, not_1_out, nor_2_out);
  Adder #(.width(15)) adder_1 (
    .a(RAM_Addres[15:1]), .b({15{1'b0}}), .out(adder_1_out), .cin(RAM_Addres[0]));  // open: cout
  Button button_1 (.out(button_1_out));
  Button button_2 (.out(button_2_out));
  Multiplexer #(.width(8), .enable("false")) multiplexer_1 (
    .in0(ram_2_data), .in1(ram_1_data), .out(RAM_output[7:0]), .sel(RAM_Addres[0]));
  RAM_part #(.addrWidth(15)) ram_1 (
    .addr(RAM_Addres[15:1]), .data(ram_1_data), .clk(nor_3_out), .ld(Get_Ram), .clr(button_1_out));  // open: sel
  RAM_part #(.addrWidth(15)) ram_2 (
    .addr(adder_1_out), .data(ram_2_data), .clk(nor_4_out), .ld(Get_Ram), .clr(button_2_out));  // open: sel
  Multiplexer #(.width(8), .enable("false")) multiplexer_2 (
    .in0(ram_1_data), .in1(ram_2_data), .out(RAM_output[15:8]), .sel(RAM_Addres[0]));
  assign ram_2_data = Set_Ram ? multiplexer_3_out : 8'bz;  // Controlled_Buffer controlled_buffer_1
  Multiplexer #(.width(8), .enable("false")) multiplexer_3 (
    .in0(RAM_input[7:0]), .in1(RAM_input[15:8]), .out(multiplexer_3_out), .sel(RAM_Addres[0]));
  Multiplexer #(.width(8), .enable("false")) multiplexer_4 (
    .in0(RAM_input[15:8]), .in1(RAM_input[7:0]), .out(multiplexer_4_out), .sel(RAM_Addres[0]));
  assign ram_1_data = Set_Ram ? multiplexer_4_out : 8'bz;  // Controlled_Buffer controlled_buffer_2
endmodule

module Central_processing_unit (
  input  Clock,
  input  Reset,
  input  [15:0] RAM_input,
  output _16_bit,
  output Get_Ram,
  output Set_Ram,
  output [15:0] RAM_output,
  output [15:0] RAM_Addres
);

  wire arithmetic_logic_unit_1_carry_out, arithmetic_logic_unit_1_overflow_out, control_unit_1__16_bit,
       control_unit_1__16_bit_2, control_unit_1_carry_in, control_unit_1_get_ram, control_unit_1_not_a,
       control_unit_1_not_b, control_unit_1_set_ram, control_unit_1_update_fs;
  wire [2:0] control_unit_1_address_reg_base, control_unit_1_alu_micro_operation;
  wire [3:0] control_unit_1_address_reg_a, control_unit_1_address_reg_b, control_unit_1_reg_address;
  wire [7:0] control_unit_1_input_fs, registery_1_fs_out;
  wire [15:0] arithmetic_logic_unit_1_result, control_unit_1_a, control_unit_1_b, control_unit_1_imidiate,
       control_unit_1_input_reg, control_unit_1_ram_output, ram_interface_1_ram_addres_2,
       ram_interface_1_ram_input_2, registery_1_output_a, registery_1_output_b, registery_1_output_base;

  RAM_interface ram_interface_1 (
    .Get_RAM_2(Get_Ram), .Set_RAM_2(Set_Ram), .RAM_input(RAM_input), .RAM_Addres(RAM_Addres),
    .RAM_output_2(RAM_output), ._16_bit(control_unit_1__16_bit_2), .Get_RAM(control_unit_1_get_ram),
    .Set_RAM(control_unit_1_set_ram), .RAM_input_2(ram_interface_1_ram_input_2),
    .Base_address(registery_1_output_base), .RAM_output(control_unit_1_ram_output), ._16_bit_2(_16_bit),
    .Imidiate_address(control_unit_1_imidiate), .RAM_Addres_2(ram_interface_1_ram_addres_2));
  Control_unit control_unit_1 (
    .Carry_In(control_unit_1_carry_in), ._16_bit(control_unit_1__16_bit), .B(control_unit_1_b),
    .A(control_unit_1_a), .ALU_Micro_Operation(control_unit_1_alu_micro_operation),
    .Result(arithmetic_logic_unit_1_result), .Carry_Out(arithmetic_logic_unit_1_carry_out),
    .Overflow_Out(arithmetic_logic_unit_1_overflow_out), .Input_FS(control_unit_1_input_fs),
    .Update_FS(control_unit_1_update_fs), .Input_Reg(control_unit_1_input_reg),
    .Reg_Address(control_unit_1_reg_address), .Output_FS(registery_1_fs_out),
    .Output_Reg_A(registery_1_output_a), .Address_Reg_A(control_unit_1_address_reg_a), .Clock(Clock),
    .RAM_output(control_unit_1_ram_output), .RAM_input(ram_interface_1_ram_input_2),
    ._16_bit_2(control_unit_1__16_bit_2), .Get_RAM(control_unit_1_get_ram), .Set_RAM(control_unit_1_set_ram),
    .Output_Reg_B(registery_1_output_b), .Address_Reg_B(control_unit_1_address_reg_b),
    .Address_Reg_Base(control_unit_1_address_reg_base), .Address(ram_interface_1_ram_addres_2),
    .Imidiate(control_unit_1_imidiate), .Not_A(control_unit_1_not_a), .Not_B(control_unit_1_not_b),
    .Reset(Reset));
  Arithmetic_logic_unit arithmetic_logic_unit_1 (
    .Carry_In(control_unit_1_carry_in), ._16_bit(control_unit_1__16_bit), .A(control_unit_1_a),
    .B(control_unit_1_b), .Micro_Operation(control_unit_1_alu_micro_operation),
    .Result(arithmetic_logic_unit_1_result), .Carry_Out(arithmetic_logic_unit_1_carry_out),
    .Overflow_Out(arithmetic_logic_unit_1_overflow_out), .Not_A(control_unit_1_not_a),
    .Not_B(control_unit_1_not_b));
  Registery registery_1 (
    .Data_in(control_unit_1_input_reg), .Input_Register(control_unit_1_reg_address),
    .FS_out(registery_1_fs_out), .FS_In(control_unit_1_input_fs), .Update_FS(control_unit_1_update_fs),
    .Base_Register(control_unit_1_address_reg_base), .Output_Base(registery_1_output_base),
    .B_Register(control_unit_1_address_reg_b), .Output_B(registery_1_output_b),
    .A_Register(control_unit_1_address_reg_a), .Output_A(registery_1_output_a), .Clock(Clock), .Reset(Reset));
endmodule

module Control_unit (
  input  Clock,
  input  Reset,
  input  [15:0] RAM_input,
  input  [15:0] Address,
  input  [15:0] Result,
  input  Carry_Out,
  input  Overflow_Out,
  input  [15:0] Output_Reg_A,
  input  [15:0] Output_Reg_B,
  input  [7:0] Output_FS,
  output Carry_In,
  output _16_bit,
  output [15:0] A,
  output _16_bit_2,
  output Not_A,
  output Get_RAM,
  output [15:0] B,
  output Set_RAM,
  output Not_B,
  output [15:0] RAM_output,
  output [2:0] ALU_Micro_Operation,
  output [15:0] Imidiate,
  output [15:0] Input_Reg,
  output [2:0] Address_Reg_Base,
  output [3:0] Address_Reg_A,
  output [3:0] Address_Reg_B,
  output [3:0] Reg_Address,
  output Update_FS,
  output [7:0] Input_FS
);

  wire and_1_out, condition_check_1_truth, Exec, Imidiate_B, Load_A, Load_B, Load_Imidiate, Load_Instruction,
       microcode_logic_1_save, microcode_logic_1_wait, Mode_A, Mode_B, multiplexer_11_out, Next, nor_1_out,
       not_1_out;
  wire [1:0] Carry_Mode;
  wire [2:0] multiplexer_2_out;
  wire [3:0] multiplexer_8_out;
  wire [15:0] Imidiate_q, Instruction_q, multiplexer_6_out;

  or or_1 (Get_RAM, Next, Load_A, Load_B);
  Register #(.width(16), .trigger("falling")) Instruction (
    .D(RAM_input), .en(Load_Instruction),
    .Q({Instruction_q[15], Imidiate_B, Instruction_q[13:11], _16_bit, Instruction_q[9:8], Mode_B, Mode_A, Instruction_q[5:0]}),
    .clk(Clock));  // open: clr
  Register #(.width(16), .trigger("falling")) u_Imidiate (
    .D(RAM_input), .en(Load_Imidiate), .Q(Imidiate_q), .clk(Clock));  // open: clr
  Multiplexer #(.width(16), .enable("false")) multiplexer_1 (.in0(Imidiate_q), .in1(16'h2), .out(Imidiate), .sel(Next));
  Control_Stage_Counter control_stage_counter_1 (
    .Clock(Clock), .B_mode(Mode_B), .Load_Instruction(Load_Instruction), .Load_Imidiate(Load_Imidiate),
    .Load_B(Load_B), .Load_A(Load_A), .Excecute_OP(Exec), .Save_A(Set_RAM), .A_mode(Mode_A),
    .Will_Save(microcode_logic_1_save), .Wait(microcode_logic_1_wait), .Reset(Reset));
  not not_1 (not_1_out, Load_B);
  Multiplexer #(.width(3), .enable("false")) multiplexer_2 (
    .in0({Instruction_q[15], Instruction_q[13:12]}), .in1({Instruction_q[11], Instruction_q[9:8]}),
    .out(multiplexer_2_out), .sel(not_1_out));
  Multiplexer #(.width(3), .enable("false")) multiplexer_3 (
    .in0(multiplexer_2_out), .in1(3'b100), .out(Address_Reg_Base), .sel(Next));
  or or_2 (Next, Load_Instruction, Load_Imidiate);
  Multiplexer #(.width(4), .enable("false")) multiplexer_4 (
    .in0({Instruction_q[11], _16_bit, Instruction_q[9:8]}), .in1(4'b1110), .out(Address_Reg_A), .sel(Mode_A));
  Multiplexer #(.width(4), .enable("false")) multiplexer_5 (
    .in0({Instruction_q[15], Imidiate_B, Instruction_q[13:12]}), .in1(4'b1111), .out(Address_Reg_B),
    .sel(Mode_B));
  Microcode_Logic microcode_logic_1 (
    .Truth(condition_check_1_truth), .Carry_mode(Carry_Mode), .Not_A(Not_A), .Not_B(Not_B),
    .ALU_mOP(ALU_Micro_Operation), .Execute(Exec), .Save(microcode_logic_1_save),
    .Wait(microcode_logic_1_wait), .OP(Instruction_q[5:0]));
  Condition_Check condition_check_1 (
    .Condition(Instruction_q[3:0]), .Flags(Output_FS), .Truth(condition_check_1_truth));
  and and_1 (and_1_out, Imidiate_B, Mode_B, Load_B);
  nor nor_1 (nor_1_out, and_1_out, Next);
  Multiplexer #(.width(16), .enable("false")) multiplexer_6 (
    .in0(Address), .in1(RAM_input), .out(multiplexer_6_out), .sel(nor_1_out));
  Multiplexer #(.width(16), .enable("false")) multiplexer_7 (
    .in0(multiplexer_6_out), .in1(Result), .out(Input_Reg), .sel(Exec));
  Multiplexer #(.width(4), .enable("false")) multiplexer_8 (
    .in0(Address_Reg_A), .in1(Address_Reg_B), .out(multiplexer_8_out), .sel(Load_B));
  Multiplexer #(.width(4), .enable("false")) multiplexer_9 (
    .in0(multiplexer_8_out), .in1(4'b1100), .out(Reg_Address), .sel(Next));
  Multiplexer #(.enable("false")) multiplexer_10 (
    .in0(Carry_Mode[0]), .in1(multiplexer_11_out), .out(Carry_In), .sel(Carry_Mode[1]));
  Multiplexer #(.enable("false")) multiplexer_11 (
    .in0(Output_FS[3]), .in1(Carry_Out), .out(multiplexer_11_out), .sel(Carry_Mode[0]));
  Value_Tester value_tester_1 (
    .Test_Reg(Result), ._16_bit(_16_bit), .Overflow(Overflow_Out), .Carry(Carry_Out), .Flags_In(Output_FS),
    .Flags_Out(Input_FS));

  assign _16_bit_2 = _16_bit;
  assign A = Output_Reg_A;
  assign B = Output_Reg_B;
  assign RAM_output = Output_Reg_A;
  assign Update_FS = 1'b0;

  // Other names for the same wires on the sheet: _16 = _16_bit; FS[7:0] = Output_FS; Ram[15:0] = RAM_input;
  //   Reg_A[3:0] = Address_Reg_A; Reg_B[3:0] = Address_Reg_B; Save_A = Set_RAM; Y[15:0] = Result
endmodule

module Registery (
  input  [3:0] B_Register,
  input  [3:0] A_Register,
  input  [2:0] Base_Register,
  input  Reset,
  input  Clock,
  input  [15:0] Data_in,
  input  [3:0] Input_Register,
  input  [7:0] FS_In,
  input  Update_FS,
  output [7:0] FS_out,
  output [15:0] Output_B,
  output [15:0] Output_A,
  output [15:0] Output_Base
);

  wire decoder_1_out0, decoder_1_out1, decoder_1_out2, decoder_1_out3, decoder_1_out4, decoder_1_out5,
       decoder_1_out6, decoder_1_out7, decoder_1_out8, decoder_1_out9, decoder_1_out12, decoder_1_out13,
       decoder_1_out14, decoder_1_out15, or_1_out, or_2_out, or_3_out, or_4_out, or_5_out;
  wire [7:0] AH_q, AL_q, BH_q, BL_q, IS_q, multiplexer_4_out, multiplexer_5_out, multiplexer_6_out;
  wire [15:0] AS_q, BS_q, CS_q, CX_q, DX_q, SS_q;

  Multiplexer #(.select(4), .width(16), .enable("false")) multiplexer_1 (
    .in0({{8{1'b0}}, AL_q}), .in1({{8{1'b0}}, AH_q}), .in2({{8{1'b0}}, BL_q}), .in3({{8{1'b0}}, BH_q}),
    .in4({AH_q, AL_q}), .in5({BH_q, BL_q}), .in6(CX_q), .in7(DX_q), .in8({{8{1'b0}}, FS_out}),
    .in9({{8{1'b0}}, IS_q}), .in10({16{1'b0}}), .in11(16'h1), .in12(CS_q), .in13(SS_q), .in14(AS_q),
    .in15(BS_q), .out(Output_B), .sel(B_Register));
  Multiplexer #(.select(4), .width(16), .enable("false")) multiplexer_2 (
    .in0({{8{1'b0}}, AL_q}), .in1({{8{1'b0}}, AH_q}), .in2({{8{1'b0}}, BL_q}), .in3({{8{1'b0}}, BH_q}),
    .in4({AH_q, AL_q}), .in5({BH_q, BL_q}), .in6(CX_q), .in7(DX_q), .in8({{8{1'b0}}, FS_out}),
    .in9({{8{1'b0}}, IS_q}), .in10({16{1'b0}}), .in11(16'h1), .in12(CS_q), .in13(SS_q), .in14(AS_q),
    .in15(BS_q), .out(Output_A), .sel(A_Register));
  Multiplexer #(.select(3), .width(16), .enable("false")) multiplexer_3 (
    .in0({AH_q, AL_q}), .in1({BH_q, BL_q}), .in2(CX_q), .in3(DX_q), .in4(CS_q), .in5(SS_q), .in6({16{1'b0}}),
    .in7(16'h1), .out(Output_Base), .sel(Base_Register));
  Register #(.width(16), .trigger("falling")) BS (
    .D(Data_in), .en(decoder_1_out15), .Q(BS_q), .clk(Clock), .clr(Reset));
  Register #(.width(16), .trigger("falling")) AS (
    .D(Data_in), .en(decoder_1_out14), .Q(AS_q), .clk(Clock), .clr(Reset));
  Register #(.width(16), .trigger("falling")) SS (
    .D(Data_in), .en(decoder_1_out13), .Q(SS_q), .clk(Clock), .clr(Reset));
  Register #(.width(16), .trigger("falling")) CS (
    .D(Data_in), .en(decoder_1_out12), .Q(CS_q), .clk(Clock), .clr(Reset));
  Register #(.trigger("falling")) IS (.D(Data_in[7:0]), .en(decoder_1_out9), .Q(IS_q), .clk(Clock), .clr(Reset));
  Multiplexer #(.width(8), .enable("false")) multiplexer_4 (
    .in0(FS_In), .in1(Data_in[7:0]), .out(multiplexer_4_out), .sel(decoder_1_out8));
  Register #(.trigger("falling")) FS (.D(multiplexer_4_out), .en(or_1_out), .Q(FS_out), .clk(Clock), .clr(Reset));
  or or_1 (or_1_out, Update_FS, decoder_1_out8);
  Register #(.width(16), .trigger("falling")) DX (.D(Data_in), .en(decoder_1_out7), .Q(DX_q), .clk(Clock), .clr(Reset));
  Register #(.width(16), .trigger("falling")) CX (.D(Data_in), .en(decoder_1_out6), .Q(CX_q), .clk(Clock), .clr(Reset));
  Multiplexer #(.width(8), .enable("false")) multiplexer_5 (
    .in0(Data_in[7:0]), .in1(Data_in[15:8]), .out(multiplexer_5_out), .sel(decoder_1_out5));
  Register #(.trigger("falling")) BH (.D(multiplexer_5_out), .en(or_2_out), .Q(BH_q), .clk(Clock), .clr(Reset));
  or or_2 (or_2_out, decoder_1_out5, decoder_1_out3);
  Register #(.trigger("falling")) BL (.D(Data_in[7:0]), .en(or_3_out), .Q(BL_q), .clk(Clock), .clr(Reset));
  Multiplexer #(.width(8), .enable("false")) multiplexer_6 (
    .in0(Data_in[7:0]), .in1(Data_in[15:8]), .out(multiplexer_6_out), .sel(decoder_1_out4));
  or or_3 (or_3_out, decoder_1_out5, decoder_1_out2);
  Register #(.trigger("falling")) AH (.D(multiplexer_6_out), .en(or_4_out), .Q(AH_q), .clk(Clock), .clr(Reset));
  or or_4 (or_4_out, decoder_1_out4, decoder_1_out1);
  Register #(.trigger("falling")) AL (.D(Data_in[7:0]), .en(or_5_out), .Q(AL_q), .clk(Clock), .clr(Reset));
  or or_5 (or_5_out, decoder_1_out4, decoder_1_out0);
  // Probe on Data_in
  Decoder #(.select(4), .disabled(0)) decoder_1 (
    .out0(decoder_1_out0), .out1(decoder_1_out1), .out2(decoder_1_out2), .out3(decoder_1_out3),
    .out4(decoder_1_out4), .out5(decoder_1_out5), .out6(decoder_1_out6), .out7(decoder_1_out7),
    .out8(decoder_1_out8), .out9(decoder_1_out9), .out12(decoder_1_out12), .out13(decoder_1_out13),
    .out14(decoder_1_out14), .out15(decoder_1_out15), .sel(Input_Register));  // open: out10, out11, en
endmodule

module Arithmetic_logic_unit (
  input  Carry_In,
  input  _16_bit,
  input  [15:0] A,
  input  Not_A,
  input  [15:0] B,
  input  Not_B,
  input  [2:0] Micro_Operation,
  output [15:0] Result,
  output Carry_Out,
  output Overflow_Out
);

  wire adder_1_cout, adder_2_cout, adder_3_cout, adder_4_cout, decoder_1_out0, decoder_1_out1,
       decoder_1_out2, decoder_1_out3, decoder_1_out4, decoder_1_out5, decoder_1_out6, decoder_1_out7,
       multiplexer_1_out, multiplexer_3_out, multiplexer_4_out, multiplexer_5_out, multiplexer_6_out,
       nand_1_out, nor_1_out, not_1_out, not_2_out, xnor_3_out, xor_2_out, xor_3_out, xor_4_out;
  wire [6:0] adder_1_out, adder_3_out, xnor_1_out, xnor_1_out_3, xnor_2_out, xnor_2_out_2;
  wire [7:7] multiplexer_2_out;
  wire [15:0] and_1_out, bit_extender_1_out, bit_extender_2_out, or_1_out, xor_1_out;
  wire [15:7] adder_2_out, xnor_1_out_2, xnor_2_out_3;

  not not_1 (not_1_out, Not_A);
  not not_2 (not_2_out, Not_B);
  Decoder #(.select(3), .enable("false")) decoder_1 (
    .out0(decoder_1_out0), .out1(decoder_1_out1), .out2(decoder_1_out2), .out3(decoder_1_out3),
    .out4(decoder_1_out4), .out5(decoder_1_out5), .out6(decoder_1_out6), .out7(decoder_1_out7),
    .sel(Micro_Operation));
  Pull_Resistor pull_resistor_1 (.node(Result));
  Pull_Resistor pull_resistor_2 (.node(Carry_Out));
  Pull_Resistor pull_resistor_3 (.node(Overflow_Out));
  nand nand_1 (nand_1_out, not_2_out, not_1_out);
  assign bit_extender_1_out = {{15{not_1_out}}, not_1_out};  // Bit_Extender bit_extender_1
  assign bit_extender_2_out = {{15{not_2_out}}, not_2_out};  // Bit_Extender bit_extender_2
  assign {xnor_1_out_2[15], xnor_1_out_3, xnor_1_out_2[7], xnor_1_out} = ~(A ^ bit_extender_1_out);  // XNOR_Gate xnor_1, 16 bits wide
  assign {xnor_2_out_3[15], xnor_2_out_2, xnor_2_out_3[7], xnor_2_out} = ~(B ^ bit_extender_2_out);  // XNOR_Gate xnor_2, 16 bits wide
  assign Result = decoder_1_out0 ? {xnor_1_out_2[15], xnor_1_out_3, xnor_1_out_2[7], xnor_1_out} : 16'bz;  // Controlled_Buffer controlled_buffer_1
  assign Result = decoder_1_out1 ? {xnor_2_out_3[15], xnor_2_out_2, xnor_2_out_3[7], xnor_2_out} : 16'bz;  // Controlled_Buffer controlled_buffer_2
  Multiplexer #(.enable("false")) multiplexer_1 (
    .in0(xnor_2_out_3[7]), .in1(xnor_2_out_3[15]), .out(multiplexer_1_out), .sel(_16_bit));
  assign Carry_Out = decoder_1_out2 ? multiplexer_1_out : 1'bz;  // Controlled_Buffer controlled_buffer_3
  assign Result = decoder_1_out2 ? {xnor_2_out_2, xnor_2_out_3[7], xnor_2_out, Carry_In} : 16'bz;  // Controlled_Buffer controlled_buffer_4
  Multiplexer #(.enable("false")) multiplexer_2 (
    .in0(Carry_In), .in1(xnor_2_out_2[0]), .out(multiplexer_2_out[7]), .sel(_16_bit));
  assign Carry_Out = decoder_1_out3 ? xnor_2_out[0] : 1'bz;  // Controlled_Buffer controlled_buffer_5
  assign Result = decoder_1_out3 ? {Carry_In, xnor_2_out_3[15], xnor_2_out_2[6:1], multiplexer_2_out[7], xnor_2_out_3[7], xnor_2_out[6:1]} : 16'bz;  // Controlled_Buffer controlled_buffer_6
  assign and_1_out = {xnor_2_out_3[15], xnor_2_out_2, xnor_2_out_3[7], xnor_2_out} & {xnor_1_out_2[15], xnor_1_out_3, xnor_1_out_2[7], xnor_1_out};  // AND_Gate and_1, 16 bits wide
  assign or_1_out = {xnor_2_out_3[15], xnor_2_out_2, xnor_2_out_3[7], xnor_2_out} | {xnor_1_out_2[15], xnor_1_out_3, xnor_1_out_2[7], xnor_1_out};  // OR_Gate or_1, 16 bits wide
  assign Result = decoder_1_out4 ? or_1_out : 16'bz;  // Controlled_Buffer controlled_buffer_7
  assign Result = decoder_1_out5 ? and_1_out : 16'bz;  // Controlled_Buffer controlled_buffer_8
  assign xor_1_out = {xnor_2_out_3[15], xnor_2_out_2, xnor_2_out_3[7], xnor_2_out} ^ {xnor_1_out_2[15], xnor_1_out_3, xnor_1_out_2[7], xnor_1_out};  // XOR_Gate xor_1, 16 bits wide
  assign Result = decoder_1_out6 ? xor_1_out : 16'bz;  // Controlled_Buffer controlled_buffer_9
  Multiplexer #(.enable("false")) multiplexer_3 (
    .in0(xnor_1_out_2[7]), .in1(xnor_1_out_2[15]), .out(multiplexer_3_out), .sel(_16_bit));
  Multiplexer #(.enable("false")) multiplexer_4 (
    .in0(xnor_2_out_3[7]), .in1(xnor_2_out_3[15]), .out(multiplexer_4_out), .sel(_16_bit));
  xor xor_2 (xor_2_out, nand_1_out, Carry_In);
  Adder #(.width(7)) adder_1 (.a(xnor_2_out), .b(xnor_1_out), .out(adder_1_out), .cin(xor_2_out), .cout(adder_1_cout));
  Adder #(.width(1)) adder_2 (
    .a(xnor_2_out_3[7]), .b(xnor_1_out_2[7]), .out(adder_2_out[7]), .cin(adder_1_cout), .cout(adder_2_cout));
  Adder #(.width(7)) adder_3 (
    .a(xnor_2_out_2), .b(xnor_1_out_3), .out(adder_3_out), .cin(adder_2_cout), .cout(adder_3_cout));
  Adder #(.width(1)) adder_4 (
    .a(xnor_2_out_3[15]), .b(xnor_1_out_2[15]), .out(adder_2_out[15]), .cin(adder_3_cout), .cout(adder_4_cout));
  // Probe on {adder_2_out[15], adder_3_out, adder_2_out[7], adder_1_out}
  // Probe on {adder_2_out[15], adder_3_out, adder_2_out[7], adder_1_out}
  xor xor_3 (xor_3_out, multiplexer_4_out, multiplexer_3_out);
  assign Result = decoder_1_out7 ? {adder_2_out[15], adder_3_out, adder_2_out[7], adder_1_out} : 16'bz;  // Controlled_Buffer controlled_buffer_10
  Multiplexer #(.enable("false")) multiplexer_5 (
    .in0(adder_1_cout), .in1(adder_3_cout), .out(multiplexer_5_out), .sel(_16_bit));
  Multiplexer #(.enable("false")) multiplexer_6 (
    .in0(adder_2_cout), .in1(adder_4_cout), .out(multiplexer_6_out), .sel(_16_bit));
  xnor xnor_3 (xnor_3_out, multiplexer_4_out, multiplexer_5_out);
  xor xor_4 (xor_4_out, nand_1_out, multiplexer_6_out);
  nor nor_1 (nor_1_out, xor_3_out, xnor_3_out);
  assign Overflow_Out = decoder_1_out7 ? nor_1_out : 1'bz;  // Controlled_Buffer controlled_buffer_11
  assign Carry_Out = decoder_1_out7 ? xor_4_out : 1'bz;  // Controlled_Buffer controlled_buffer_12

  // Notes on the sheet:
  //   PASS A
  //   PASS B
  //   LSH
  //   RSH
  //   OR
  //   AND
  //   XOR
  //   ADD
endmodule

module RAM_interface (
  input  _16_bit,
  input  Get_RAM,
  input  Set_RAM,
  input  [15:0] RAM_input,
  input  [15:0] RAM_output,
  input  [15:0] Base_address,
  input  [15:0] Imidiate_address,
  output _16_bit_2,
  output Get_RAM_2,
  output Set_RAM_2,
  output [15:0] RAM_input_2,
  output [15:0] RAM_output_2,
  output [15:0] RAM_Addres,
  output [15:0] RAM_Addres_2
);

  wire not_2_out, not_3_out, not_5_out, not_6_out, not_7_out, not_8_out, not_9_out, not_10_out, not_11_out,
       not_12_out, not_13_out, not_14_out, not_15_out, not_16_out;

  not not_1 (Get_RAM_2, not_2_out);
  not not_2 (not_2_out, not_5_out);
  not not_3 (not_3_out, not_8_out);
  not not_4 (Set_RAM_2, not_3_out);
  not not_5 (not_5_out, not_6_out);
  not not_6 (not_6_out, not_9_out);
  not not_7 (not_7_out, not_12_out);
  not not_8 (not_8_out, not_7_out);
  not not_9 (not_9_out, not_10_out);
  not not_10 (not_10_out, not_13_out);
  not not_11 (not_11_out, not_16_out);
  not not_12 (not_12_out, not_11_out);
  Adder #(.width(16)) adder_1 (.a(Base_address), .b(Imidiate_address), .out(RAM_Addres));  // open: cin, cout
  not not_13 (not_13_out, not_14_out);
  not not_14 (not_14_out, Get_RAM);
  not not_15 (not_15_out, Set_RAM);
  not not_16 (not_16_out, not_15_out);

  assign _16_bit_2 = _16_bit;
  assign RAM_Addres_2 = RAM_Addres;
  assign RAM_input_2 = RAM_input;
  assign RAM_output_2 = RAM_output;
endmodule

module Value_Tester (
  input  Overflow,
  input  Carry,
  input  [7:0] Flags_In,
  input  [15:0] Test_Reg,
  input  _16_bit,
  output [7:0] Flags_Out
);

  nor nor_1 (Flags_Out[0], Test_Reg[0], Test_Reg[1], Test_Reg[2], Test_Reg[3], Test_Reg[4], Test_Reg[5], Test_Reg[6], Test_Reg[7], Test_Reg[8], Test_Reg[9], Test_Reg[10], Test_Reg[11], Test_Reg[12], Test_Reg[13], Test_Reg[14], Test_Reg[15]);
  Multiplexer #(.enable("false")) multiplexer_1 (
    .in0(Test_Reg[7]), .in1(Test_Reg[15]), .out(Flags_Out[1]), .sel(_16_bit));
  not not_1 (Flags_Out[2], Test_Reg[0]);

  assign Flags_Out[7:3] = {Flags_In[7:5], Overflow, Carry};
endmodule

module Condition_Check (
  input  [3:0] Condition,
  input  [7:0] Flags,
  output Truth
);

  wire controlled_buffer_1_out, decoder_1_out0, decoder_1_out1, decoder_1_out2, decoder_1_out3,
       decoder_1_out4, decoder_1_out5, decoder_1_out6, decoder_1_out7, nor_1_out, not_1_out;

  Decoder #(.select(3)) decoder_1 (
    .out0(decoder_1_out0), .out1(decoder_1_out1), .out2(decoder_1_out2), .out3(decoder_1_out3),
    .out4(decoder_1_out4), .out5(decoder_1_out5), .out6(decoder_1_out6), .out7(decoder_1_out7),
    .sel(Condition[3:1]));  // open: en
  not not_1 (not_1_out, Flags[1]);
  nor nor_1 (nor_1_out, not_1_out, Flags[0]);
  assign controlled_buffer_1_out = decoder_1_out0 ? Flags[0] : 1'bz;  // Controlled_Buffer controlled_buffer_1
  assign controlled_buffer_1_out = decoder_1_out1 ? Flags[1] : 1'bz;  // Controlled_Buffer controlled_buffer_2
  assign controlled_buffer_1_out = decoder_1_out2 ? Flags[2] : 1'bz;  // Controlled_Buffer controlled_buffer_3
  assign controlled_buffer_1_out = decoder_1_out3 ? Flags[3] : 1'bz;  // Controlled_Buffer controlled_buffer_4
  assign controlled_buffer_1_out = decoder_1_out4 ? Flags[4] : 1'bz;  // Controlled_Buffer controlled_buffer_5
  assign controlled_buffer_1_out = decoder_1_out5 ? nor_1_out : 1'bz;  // Controlled_Buffer controlled_buffer_6
  assign controlled_buffer_1_out = decoder_1_out6 ? 1'b1 : 1'bz;  // Controlled_Buffer controlled_buffer_7
  assign controlled_buffer_1_out = decoder_1_out7 ? 1'b1 : 1'bz;  // Controlled_Buffer controlled_buffer_8
  xor xor_1 (Truth, Condition[0], controlled_buffer_1_out);
endmodule

module Control_Stage_Counter (
  input  Clock,
  input  Reset,
  input  B_mode,
  input  A_mode,
  input  Will_Save,
  input  Wait,
  output Load_Instruction,
  output Load_Imidiate,
  output Load_B,
  output Load_A,
  output Excecute_OP,
  output Save_A
);

  wire and_1_out, demultiplexer_1_out0, demultiplexer_1_out1, demultiplexer_2_out0, demultiplexer_2_out1,
       demultiplexer_3_out0, demultiplexer_3_out1, nor_1_out, nor_2_out, or_1_out, or_2_out, or_3_out;

  nor nor_1 (nor_1_out, and_1_out, Load_A, Load_B, Load_Imidiate, Load_Instruction);
  nor nor_2 (nor_2_out, Wait, ~Clock);  // NOR_Gate
  D_Flip_Flop d_ff_1 (.clk(nor_2_out), .D(nor_1_out), .Q(Load_Instruction), .reset(Reset));  // open: Qn, preset, en
  Demultiplexer #(.enable("false")) demultiplexer_1 (
    .out0(demultiplexer_1_out0), .out1(demultiplexer_1_out1), .in(Load_Instruction), .sel(or_1_out));
  or or_1 (or_1_out, A_mode, B_mode);
  D_Flip_Flop d_ff_2 (
    .clk(nor_2_out), .D(demultiplexer_1_out1), .Q(Load_Imidiate), .reset(Reset));  // open: Qn, preset, en
  Demultiplexer #(.enable("false")) demultiplexer_2 (
    .out0(demultiplexer_2_out0), .out1(demultiplexer_2_out1), .in(Load_Imidiate), .sel(B_mode));
  D_Flip_Flop d_ff_3 (.clk(nor_2_out), .D(demultiplexer_2_out1), .Q(Load_B), .reset(Reset));  // open: Qn, preset, en
  Demultiplexer #(.enable("false")) demultiplexer_3 (
    .out0(demultiplexer_3_out0), .out1(demultiplexer_3_out1), .in(Load_B), .sel(A_mode));
  or or_2 (or_2_out, demultiplexer_3_out1, demultiplexer_2_out0);
  D_Flip_Flop d_ff_4 (.clk(nor_2_out), .D(or_2_out), .Q(Load_A), .reset(Reset));  // open: Qn, preset, en
  D_Flip_Flop d_ff_5 (.clk(nor_2_out), .D(or_3_out), .Q(Excecute_OP), .reset(Reset));  // open: Qn, preset, en
  or or_3 (or_3_out, demultiplexer_1_out0, demultiplexer_3_out0, Load_A);
  and and_1 (and_1_out, Excecute_OP, A_mode, Will_Save);
  D_Flip_Flop d_ff_6 (.clk(nor_2_out), .D(and_1_out), .Q(Save_A), .reset(Reset));  // open: Qn, preset, en
endmodule

module Microcode_Logic (
  input  Execute,
  input  [5:0] OP,
  input  Truth,
  output Save,
  output Wait,
  output [1:0] Carry_mode,
  output Not_A,
  output Not_B,
  output [2:0] ALU_mOP
);

  wire and_2_out, multiplexer_1_out, nor_1_out, not_1_out;
  wire [0:0] not_2_out;
  wire [6:0] multiplexer_2_out, multiplexer_3_out, multiplexer_4_out;

  or or_1 (Save, multiplexer_1_out, OP[5]);
  Multiplexer #(.enable("false")) multiplexer_1 (.in0(Truth), .in1(1'b0), .out(multiplexer_1_out), .sel(OP[4]));
  not not_1 (not_1_out, OP[4]);
  and and_1 (Wait, Execute, and_2_out);
  and and_2 (and_2_out, nor_1_out, 1'b0);
  nor nor_1 (nor_1_out, not_1_out, OP[5]);
  not not_2 (not_2_out[0], OP[2]);
  Multiplexer #(.width(7), .enable("false")) multiplexer_2 (
    .in0({{6{1'b0}}, Truth}), .in1({7{1'b0}}), .out(multiplexer_2_out), .sel(OP[4]));
  Multiplexer #(.width(7), .enable("false")) multiplexer_3 (
    .in0({2'b00, OP[1:0], 1'b1, OP[3:2]}), .in1(multiplexer_4_out), .out(multiplexer_3_out), .sel(OP[4]));
  Multiplexer #(.width(7), .enable("false")) multiplexer_4 (
    .in0({OP[2], not_2_out[0], OP[1:0], 3'b111}), .in1({OP[1:0], 4'b0001, OP[2]}), .out(multiplexer_4_out),
    .sel(OP[3]));
  Multiplexer #(.width(7), .enable("false")) multiplexer_5 (
    .in0(multiplexer_2_out), .in1(multiplexer_3_out), .out({Carry_mode, Not_B, Not_A, ALU_mOP}), .sel(OP[5]));
  // Probe on OP

  // Notes on the sheet:
  //   TODO: special operations
endmodule

module Pre_Loader (
  input  Clock,
  input  Reset,
  output Loaded,
  output [15:0] Address,
  output [15:0] Data,
  output Set_RAM
);

  wire comparator_1_eq, not_1_out, not_2_out;

  not not_1 (not_1_out, comparator_1_eq);
  and and_1 (Set_RAM, Clock, ~Loaded);  // AND_Gate
  not not_2 (not_2_out, Clock);
  Comparator #(.width(16)) comparator_1 (.a(16'h20), .b(Address), .eq(comparator_1_eq));  // open: gt, lt
  Counter #(.width(16), .max('hffff), .trigger("falling")) counter_1 (
    .count(not_1_out), .Q(Address), .clk(Clock), .clr(Reset));  // open: load, D, carry
  D_Flip_Flop d_ff_1 (.clk(not_2_out), .D(comparator_1_eq), .Q(Loaded));  // open: Qn, preset, en, reset
  ROM #(.addrWidth(16)) rom_1 (.addr(Address), .data(Data[7:0]));  // open: sel

  assign Data[15:8] = {8{1'b0}};

  // Notes on the sheet:
  //   contents of rom_1 (hex, n*v repeats v):
  //   0 0 2c b0 4e 0 0 1 87 ec 0 0 8e ec 0 a
endmodule
